// Logisim project mips-like.circ as structural Verilog: 6 circuits, main circuit PROCESSADOR
module PROCESSADOR (
  output [31:0] \INSTRUÇÃO ,
  output [31:0] \INSTRUÇÃO_2 ,
  output [31:0] \INSTRUÇÃO_3 ,
  output [7:0] \INSTRUÇÃO_4 
);

  wire button_1_out, clock_1_out, liga_menoria_1_out_3, UC_j, UC_li, UC_read_mer, UC_write_mer, UC_write_reg,
       ula_1_bge;
  wire [3:0] UC_ula_op;
  wire [7:0] PC_q_2;
  wire [31:0] adder_1_out, converte_8_para_32_1_out_2, converte_8_para_32_2_out_2,
       converte_8_para_32_3_out_2, multiplexer_1_out, multiplexer_2_out, multiplexer_3_out, PC_q,
       ula_1_ula_out;

  Adder #(.width(32)) adder_1 (.a({PC_q[31:10], PC_q_2, PC_q[1:0]}), .b(32'h4), .out(adder_1_out));  // open: cin, cout
  Multiplexer #(.width(32), .enable("false")) multiplexer_1 (
    .in0(adder_1_out), .in1(converte_8_para_32_2_out_2), .out(multiplexer_1_out), .sel(UC_j));
  Register #(.width(32)) PC (
    .D(multiplexer_2_out), .Q({PC_q[31:10], PC_q_2, PC_q[1:0]}), .clk(clock_1_out), .clr(button_1_out));  // open: en
  Clock clock_1 (.out(clock_1_out));
  Button button_1 (.out(button_1_out));
  Multiplexer #(.width(32), .enable("false")) multiplexer_2 (
    .in0(multiplexer_1_out), .in1(converte_8_para_32_1_out_2), .out(multiplexer_2_out), .sel(ula_1_bge));
  converte_8_para_32 converte_8_para_32_1 (.out_2(converte_8_para_32_1_out_2), .in_1(\INSTRUÇÃO_3 [15:8]));
  converte_8_para_32 converte_8_para_32_2 (.out_2(converte_8_para_32_2_out_2), .in_1(\INSTRUÇÃO_3 [27:20]));
  ROM #(.dataWidth(32)) rom_1 (.addr(PC_q_2), .data(\INSTRUÇÃO_3 ));  // open: sel
  UC UC (
    .write_reg(UC_write_reg), .ula_op(UC_ula_op), .E0(\INSTRUÇÃO_3 [31]), .E1(\INSTRUÇÃO_3 [30]),
    .E2(\INSTRUÇÃO_3 [29]), .E3(\INSTRUÇÃO_3 [28]), .read_mer(UC_read_mer), .write_mer(UC_write_mer),
    .li(UC_li), .J(UC_j));
  converte_8_para_32 converte_8_para_32_3 (.out_2(converte_8_para_32_3_out_2), .in_1(\INSTRUÇÃO_3 [23:16]));
  BANCO_DE_REGISTRADORES banco_de_registradores_1 (
    .DATA_WRITE(multiplexer_3_out), .CLK(clock_1_out), .RW(\INSTRUÇÃO_3 [27:24]), .R0_D(\INSTRUÇÃO ),
    .R0(\INSTRUÇÃO_3 [19:16]), .R1_D(\INSTRUÇÃO_2 ), .R1(\INSTRUÇÃO_3 [23:20]), .RW_2(UC_write_reg),
    .RESET(button_1_out));
  Multiplexer #(.width(32), .enable("false")) multiplexer_3 (
    .in0(ula_1_ula_out), .in1(converte_8_para_32_3_out_2), .out(multiplexer_3_out), .sel(UC_li));
  ULA ula_1 (
    .DATA_0(\INSTRUÇÃO ), .DATA_1(\INSTRUÇÃO_2 ), .ULA_OUT(ula_1_ula_out), .ULA_OP(UC_ula_op), .BGE(ula_1_bge));
  liga_menoria liga_menoria_1 (.in_1(UC_write_mer), .in_2(UC_read_mer), .out_3(liga_menoria_1_out_3));
  Multiplexer #(.width(32), .enable("false")) multiplexer_4 (
    .in1(\INSTRUÇÃO_2 ), .out(ula_1_ula_out), .sel(UC_write_mer));  // open: in0
  RAM #(.addrWidth(6), .dataWidth(32)) ram_1 (
    .addr(\INSTRUÇÃO [7:2]), .data(ula_1_ula_out), .sel(liga_menoria_1_out_3), .clk(clock_1_out),
    .ld(UC_read_mer));  // open: clr

  assign \INSTRUÇÃO_4  = \INSTRUÇÃO [7:0];

  // Notes on the sheet:
  //   REG_0
  //   REG_1
  //   REG_W
  //   contents of rom_1 (hex, n*v repeats v):
  //   41010000 42040000 43000000 44100000 4e200000 4f100000 45000000 20529400 46000000 20628c00 47000000
  //   4c000000 20727400 ba5f0000 bd720000 9aad0000 9aa30000 c80a0000 ba7f0000 bd620000 9aad0000 9aa40000
  //   c90a0000 bd890000 9ccd0000 97710000 13000000 ba7f0000 bd620000 9aad0000 9aae0000 30ca0000 96610000
  //   12800000 95510000 12000000
  //   DATA_W
  //   BANCO DE REGISTRADORES
  //   REG0_D
  //   REG1_D
  //   ULA
endmodule

module ULA (
  input  [31:0] DATA_1,
  input  [31:0] DATA_0,
  input  [3:0] ULA_OP,
  output BGE,
  output [31:0] ULA_OUT
);

  wire and_1_out, comparator_1_eq, comparator_1_lt, or_1_out;
  wire [31:0] adder_1_out, multiplier_1_out, subtractor_1_out;

  Comparator #(.width(32), .mode("unsigned")) comparator_1 (
    .a(DATA_0), .b(DATA_1), .eq(comparator_1_eq), .lt(comparator_1_lt));  // open: gt
  Adder #(.width(32)) adder_1 (.a(DATA_0), .b(DATA_1), .out(adder_1_out));  // open: cin, cout
  Subtractor #(.width(32)) subtractor_1 (.a(DATA_0), .b(DATA_1), .out(subtractor_1_out));  // open: bin, bout
  Multiplier #(.width(32)) multiplier_1 (.a(DATA_0), .b(DATA_1), .out(multiplier_1_out));  // open: cin, cout
  or or_1 (or_1_out, comparator_1_lt, comparator_1_eq);
  Multiplexer #(.select(4), .width(32), .enable("false")) multiplexer_1 (
    .in9(adder_1_out), .in10(subtractor_1_out), .in11(multiplier_1_out), .out(ULA_OUT), .sel(ULA_OP));  // open: in0, in1, in2, in3, in4, in5, in6, in7, in8, in12, in13, in14, in15
  and and_1 (and_1_out, ~ULA_OP[0], ULA_OP[1], ~ULA_OP[2], ~ULA_OP[3]);  // AND_Gate
  and and_2 (BGE, or_1_out, and_1_out);
endmodule

module UC (
  input  E0,
  input  E1,
  input  E2,
  input  E3,
  output write_reg,
  output [3:0] ula_op,
  output read_mer,
  output write_mer,
  output li,
  output J
);

  or or_1 (write_reg, E1, E0);
  and and_1 (read_mer, E0, E1);
  and and_2 (write_mer, ~E0, ~E1, E2, E3);  // AND_Gate
  and and_3 (li, ~E3, ~E2, E1, ~E0);  // AND_Gate
  and and_4 (J, E3, ~E2, ~E1, ~E0);  // AND_Gate

  assign ula_op = {E0, E1, E2, E3};
endmodule

module BANCO_DE_REGISTRADORES (
  input  [31:0] DATA_WRITE,
  input  [3:0] R0,
  input  CLK,
  input  [3:0] R1,
  input  [3:0] RW,
  input  RESET,
  input  RW_2,
  output [31:0] R0_D,
  output [31:0] R1_D
);

  wire demultiplexer_1_out0, demultiplexer_1_out1, demultiplexer_1_out2, demultiplexer_1_out3,
       demultiplexer_1_out4, demultiplexer_1_out5, demultiplexer_1_out6, demultiplexer_1_out7,
       demultiplexer_1_out8, demultiplexer_1_out9, demultiplexer_1_out10, demultiplexer_1_out11,
       demultiplexer_1_out12, demultiplexer_1_out13, demultiplexer_1_out14, demultiplexer_1_out15;
  wire [31:0] register_1_q, register_2_q, register_3_q, register_4_q, register_5_q, register_6_q,
       register_7_q, register_8_q, register_9_q, register_10_q, register_11_q, register_12_q, register_13_q,
       register_14_q, register_15_q, register_16_q;

  Demultiplexer #(.select(4), .enable("false")) demultiplexer_1 (
    .out0(demultiplexer_1_out0), .out1(demultiplexer_1_out1), .out2(demultiplexer_1_out2),
    .out3(demultiplexer_1_out3), .out4(demultiplexer_1_out4), .out5(demultiplexer_1_out5),
    .out6(demultiplexer_1_out6), .out7(demultiplexer_1_out7), .out8(demultiplexer_1_out8),
    .out9(demultiplexer_1_out9), .out10(demultiplexer_1_out10), .out11(demultiplexer_1_out11),
    .out12(demultiplexer_1_out12), .out13(demultiplexer_1_out13), .out14(demultiplexer_1_out14),
    .out15(demultiplexer_1_out15), .in(RW_2), .sel(RW));
  Register #(.width(32)) register_1 (
    .D(DATA_WRITE), .en(demultiplexer_1_out0), .Q(register_1_q), .clk(CLK), .clr(RESET));
  Register #(.width(32)) register_2 (
    .D(DATA_WRITE), .en(demultiplexer_1_out1), .Q(register_2_q), .clk(CLK), .clr(RESET));
  Register #(.width(32)) register_3 (
    .D(DATA_WRITE), .en(demultiplexer_1_out2), .Q(register_3_q), .clk(CLK), .clr(RESET));
  Register #(.width(32)) register_4 (
    .D(DATA_WRITE), .en(demultiplexer_1_out3), .Q(register_4_q), .clk(CLK), .clr(RESET));
  Register #(.width(32)) register_5 (
    .D(DATA_WRITE), .en(demultiplexer_1_out4), .Q(register_5_q), .clk(CLK), .clr(RESET));
  Register #(.width(32)) register_6 (
    .D(DATA_WRITE), .en(demultiplexer_1_out5), .Q(register_6_q), .clk(CLK), .clr(RESET));
  Register #(.width(32)) register_7 (
    .D(DATA_WRITE), .en(demultiplexer_1_out6), .Q(register_7_q), .clk(CLK), .clr(RESET));
  Register #(.width(32)) register_8 (
    .D(DATA_WRITE), .en(demultiplexer_1_out7), .Q(register_8_q), .clk(CLK), .clr(RESET));
  Register #(.width(32)) register_9 (
    .D(DATA_WRITE), .en(demultiplexer_1_out8), .Q(register_9_q), .clk(CLK), .clr(RESET));
  Register #(.width(32)) register_10 (
    .D(DATA_WRITE), .en(demultiplexer_1_out9), .Q(register_10_q), .clk(CLK), .clr(RESET));
  Register #(.width(32)) register_11 (
    .D(DATA_WRITE), .en(demultiplexer_1_out10), .Q(register_11_q), .clk(CLK), .clr(RESET));
  Register #(.width(32)) register_12 (
    .D(DATA_WRITE), .en(demultiplexer_1_out11), .Q(register_12_q), .clk(CLK), .clr(RESET));
  Register #(.width(32)) register_13 (
    .D(DATA_WRITE), .en(demultiplexer_1_out12), .Q(register_13_q), .clk(CLK), .clr(RESET));
  Register #(.width(32)) register_14 (
    .D(DATA_WRITE), .en(demultiplexer_1_out13), .Q(register_14_q), .clk(CLK), .clr(RESET));
  Register #(.width(32)) register_15 (
    .D(DATA_WRITE), .en(demultiplexer_1_out14), .Q(register_15_q), .clk(CLK), .clr(RESET));
  Register #(.width(32)) register_16 (
    .D(DATA_WRITE), .en(demultiplexer_1_out15), .Q(register_16_q), .clk(CLK), .clr(RESET));
  Multiplexer #(.select(4), .width(32), .disabled(0), .enable("false")) multiplexer_1 (
    .in0(register_1_q), .in1(register_2_q), .in2(register_3_q), .in3(register_4_q), .in4(register_5_q),
    .in5(register_6_q), .in6(register_7_q), .in7(register_8_q), .in8(register_9_q), .in9(register_10_q),
    .in10(register_11_q), .in11(register_12_q), .in12(register_13_q), .in13(register_14_q),
    .in14(register_15_q), .in15(register_16_q), .out(R0_D), .sel(R0));
  Multiplexer #(.select(4), .width(32), .enable("false")) multiplexer_2 (
    .in0(register_1_q), .in1(register_2_q), .in2(register_3_q), .in3(register_4_q), .in4(register_5_q),
    .in5(register_6_q), .in6(register_7_q), .in7(register_8_q), .in8(register_9_q), .in9(register_10_q),
    .in10(register_11_q), .in11(register_12_q), .in12(register_13_q), .in13(register_14_q),
    .in14(register_15_q), .in15(register_16_q), .out(R1_D), .sel(R1));
endmodule

module converte_8_para_32 (
  input  [7:0] in_1,
  output [31:0] out_2
);


  assign out_2 = {{24{1'b0}}, in_1};
endmodule

module liga_menoria (
  input  in_1,
  input  in_2,
  output out_3
);

  or or_1 (out_3, in_1, in_2);
endmodule
